// Logisim project contador_senha.circ as structural Verilog: 1 circuit, main circuit main
module main (
  input  [2:0] s,
  input  add,
  output cont_end
);

  wire and_1_out, and_2_out, clock_out, j_k_ff_1_q, j_k_ff_2_q, not_1_out, not_2_out;

  Clock clock (.out(clock_out));
  not not_1 (not_1_out, s[0]);
  and and_1 (and_1_out, not_1_out, s[1], not_2_out);
  not not_2 (not_2_out, s[2]);
  and and_2 (and_2_out, and_1_out, add);
  J_K_Flip_Flop #(.NegatePresetClear("true")) j_k_ff_1 (
    .J(1'b1), .clk(clock_out), .K(1'b1), .Q(j_k_ff_1_q), .preset(1'b1), .reset(and_2_out));  // open: Qn
  J_K_Flip_Flop #(.NegatePresetClear("true")) j_k_ff_2 (
    .J(j_k_ff_1_q), .clk(clock_out), .K(j_k_ff_1_q), .Q(j_k_ff_2_q), .preset(1'b1), .reset(and_2_out));  // open: Qn
  and and_3 (cont_end, j_k_ff_2_q, j_k_ff_1_q);
endmodule
